// Logisim project Somador 4 bits completo_7segmentos.circ as structural Verilog: 3 circuits, main circuit main
module main (
  input  A4,
  input  A3,
  input  A2,
  input  A1,
  input  C0,
  input  B4,
  input  B3,
  input  B2,
  input  B1,
  output C4
);

  wire meu_decodificador_1_a, meu_decodificador_1_b, meu_decodificador_1_c, meu_decodificador_1_d,
       meu_decodificador_1_e, meu_decodificador_1_f, meu_decodificador_1_g, meu_decodificador_2_a,
       meu_decodificador_2_b, meu_decodificador_2_c, meu_decodificador_2_d, meu_decodificador_2_e,
       meu_decodificador_2_f, meu_decodificador_2_g, meu_decodificador_3_a, meu_decodificador_3_b,
       meu_decodificador_3_c, meu_decodificador_3_d, meu_decodificador_3_e, meu_decodificador_3_f,
       meu_decodificador_3_g, somador_4_bits_completo_1_s1, somador_4_bits_completo_1_s2,
       somador_4_bits_completo_1_s3, somador_4_bits_completo_1_s4;

  Meu_decodificador meu_decodificador_1 (
    .S0(A4), .S1(A3), .S2(A2), .S3(A1), .A(meu_decodificador_1_a), .B(meu_decodificador_1_b),
    .C(meu_decodificador_1_c), .D(meu_decodificador_1_d), .E(meu_decodificador_1_e),
    .F(meu_decodificador_1_f), .G(meu_decodificador_1_g));
  Meu_decodificador meu_decodificador_2 (
    .S0(B4), .S1(B3), .S2(B2), .S3(B1), .A(meu_decodificador_2_a), .B(meu_decodificador_2_b),
    .C(meu_decodificador_2_c), .D(meu_decodificador_2_d), .E(meu_decodificador_2_e),
    .F(meu_decodificador_2_f), .G(meu_decodificador_2_g));
  _7_Segment_Display u_7_segment_display_1 (
    .g(meu_decodificador_1_g), .f(meu_decodificador_1_f), .a(meu_decodificador_1_a),
    .b(meu_decodificador_1_b), .e(meu_decodificador_1_e), .d(meu_decodificador_1_d), .c(meu_decodificador_1_c));  // open: dp
  _7_Segment_Display u_7_segment_display_2 (
    .g(meu_decodificador_2_g), .f(meu_decodificador_2_f), .a(meu_decodificador_2_a),
    .b(meu_decodificador_2_b), .e(meu_decodificador_2_e), .d(meu_decodificador_2_d), .c(meu_decodificador_2_c));  // open: dp
  Somador_4_bits_Completo somador_4_bits_completo_1 (
    .B4(B4), .A4(A4), .B3(B3), .A3(A3), .B2(B2), .A2(A2), .B1(B1), .A1(A1), .C0(C0), .C4(C4),
    .S4(somador_4_bits_completo_1_s4), .S3(somador_4_bits_completo_1_s3), .S2(somador_4_bits_completo_1_s2),
    .S1(somador_4_bits_completo_1_s1));
  Meu_decodificador meu_decodificador_3 (
    .S0(somador_4_bits_completo_1_s4), .S1(somador_4_bits_completo_1_s3), .S2(somador_4_bits_completo_1_s2),
    .S3(somador_4_bits_completo_1_s1), .A(meu_decodificador_3_a), .B(meu_decodificador_3_b),
    .C(meu_decodificador_3_c), .D(meu_decodificador_3_d), .E(meu_decodificador_3_e),
    .F(meu_decodificador_3_f), .G(meu_decodificador_3_g));
  _7_Segment_Display u_7_segment_display_3 (
    .g(meu_decodificador_3_g), .f(meu_decodificador_3_f), .a(meu_decodificador_3_a),
    .b(meu_decodificador_3_b), .e(meu_decodificador_3_e), .d(meu_decodificador_3_d), .c(meu_decodificador_3_c));  // open: dp
endmodule

module Somador_4_bits_Completo (
  input  B4,
  input  A4,
  input  B3,
  input  A3,
  input  B2,
  input  A2,
  input  B1,
  input  A1,
  input  C0,
  output C4,
  output S4,
  output S3,
  output S2,
  output S1
);

  wire and_1_out, and_2_out, and_3_out, and_4_out, and_5_out, and_6_out, and_7_out, and_8_out, and_9_out,
       and_10_out, and_11_out, and_12_out, and_13_out, and_14_out, buffer_1_out, buffer_2_out, buffer_3_out,
       buffer_4_out, nand_1_out, nand_2_out, nand_3_out, nand_4_out, nor_1_out, nor_2_out, nor_3_out,
       nor_4_out, nor_6_out, nor_7_out, nor_8_out, not_1_out, not_2_out;

  nand nand_1 (nand_1_out, B4, A4);
  nor nor_1 (nor_1_out, B4, A4);
  nand nand_2 (nand_2_out, B3, A3);
  nor nor_2 (nor_2_out, B3, A3);
  nand nand_3 (nand_3_out, B2, A2);
  nor nor_3 (nor_3_out, B2, A2);
  nand nand_4 (nand_4_out, B1, A1);
  nor nor_4 (nor_4_out, B1, A1);
  not not_1 (not_1_out, C0);
  buf buffer_1 (buffer_1_out, nor_1_out);
  and and_1 (and_1_out, nor_2_out, nand_1_out);
  and and_2 (and_2_out, nor_3_out, nand_1_out, nand_2_out);
  and and_3 (and_3_out, nor_4_out, nand_1_out, nand_2_out, nand_3_out);
  and and_4 (and_4_out, nand_1_out, nand_2_out, nand_3_out, nand_4_out, not_1_out);
  and and_5 (and_5_out, nand_1_out, ~nor_1_out);  // AND_Gate
  buf buffer_2 (buffer_2_out, nor_2_out);
  and and_6 (and_6_out, nor_3_out, nand_2_out);
  and and_7 (and_7_out, nor_4_out, nand_2_out, nand_3_out);
  and and_8 (and_8_out, nand_2_out, nand_3_out, nand_4_out, not_1_out);
  and and_9 (and_9_out, nand_2_out, ~nor_2_out);  // AND_Gate
  buf buffer_3 (buffer_3_out, nor_3_out);
  and and_10 (and_10_out, nor_4_out, nand_3_out);
  and and_11 (and_11_out, nand_3_out, nand_4_out, not_1_out);
  and and_12 (and_12_out, nand_3_out, ~nor_3_out);  // AND_Gate
  buf buffer_4 (buffer_4_out, nor_4_out);
  and and_13 (and_13_out, nand_4_out, not_1_out);
  and and_14 (and_14_out, nand_4_out, ~nor_4_out);  // AND_Gate
  not not_2 (not_2_out, not_1_out);
  nor nor_5 (C4, buffer_1_out, and_1_out, and_2_out, and_3_out, and_4_out);
  nor nor_6 (nor_6_out, buffer_2_out, and_6_out, and_7_out, and_8_out);
  nor nor_7 (nor_7_out, buffer_3_out, and_10_out, and_11_out);
  nor nor_8 (nor_8_out, buffer_4_out, and_13_out);
  xor xor_1 (S4, and_5_out, nor_6_out);
  xor xor_2 (S3, and_9_out, nor_7_out);
  xor xor_3 (S2, and_12_out, nor_8_out);
  xor xor_4 (S1, and_14_out, not_2_out);
endmodule

module Meu_decodificador (
  input  S0,
  input  S1,
  input  S2,
  input  S3,
  output A,
  output B,
  output C,
  output D,
  output E,
  output F,
  output G
);

  wire and_1_out, and_2_out, and_3_out, and_4_out, and_5_out, and_6_out, and_7_out, and_8_out, and_9_out,
       and_10_out, and_11_out, and_12_out, and_13_out, and_14_out, and_15_out, and_16_out, and_17_out,
       and_18_out, and_19_out, and_20_out, and_21_out, and_22_out, and_23_out, and_24_out, and_25_out,
       and_26_out, and_27_out, and_28_out, and_29_out, and_30_out, and_31_out, and_32_out, and_33_out,
       and_34_out, and_35_out, and_36_out, and_37_out, and_38_out, and_39_out, and_40_out, and_41_out,
       and_42_out, and_43_out, and_44_out, and_45_out, and_46_out, not_1_out, not_2_out, not_3_out,
       not_4_out, not_5_out, not_6_out, not_7_out, not_8_out, not_9_out, not_10_out, not_11_out, not_12_out,
       not_13_out, not_14_out, not_15_out, not_16_out, not_17_out, not_18_out, not_19_out, not_20_out,
       not_21_out, not_22_out, not_23_out, not_24_out, not_25_out, not_26_out, not_27_out, not_28_out,
       not_29_out, not_30_out, not_31_out, not_32_out, not_33_out, not_34_out, not_35_out, not_36_out,
       not_37_out, not_38_out, not_39_out, not_40_out, not_41_out, not_42_out, not_43_out, or_1_out,
       or_2_out, or_3_out, or_4_out, or_5_out, or_6_out, or_7_out, or_8_out, or_9_out, or_10_out, or_12_out,
       or_13_out, or_14_out, or_15_out, or_16_out, or_17_out, or_18_out, or_20_out, or_21_out, or_22_out,
       or_23_out;

  not not_1 (not_1_out, S1);
  not not_2 (not_2_out, S3);
  not not_3 (not_3_out, S0);
  not not_4 (not_4_out, S0);
  and and_1 (and_1_out, S0, not_5_out);
  not not_5 (not_5_out, S1);
  not not_6 (not_6_out, S2);
  not not_7 (not_7_out, S0);
  not not_8 (not_8_out, S1);
  not not_9 (not_9_out, S0);
  and and_2 (and_2_out, not_9_out, not_10_out);
  not not_10 (not_10_out, S2);
  not not_11 (not_11_out, S3);
  not not_12 (not_12_out, S0);
  not not_13 (not_13_out, S2);
  not not_14 (not_14_out, S0);
  and and_3 (and_3_out, not_14_out, not_15_out);
  not not_15 (not_15_out, S2);
  not not_16 (not_16_out, S0);
  and and_4 (and_4_out, not_16_out, S3);
  not not_17 (not_17_out, S2);
  not not_18 (not_18_out, S0);
  not not_19 (not_19_out, S1);
  not not_20 (not_20_out, S0);
  and and_5 (and_5_out, not_20_out, not_21_out);
  not not_21 (not_21_out, S1);
  not not_22 (not_22_out, S3);
  not not_23 (not_23_out, S1);
  and and_6 (and_6_out, not_23_out, S2);
  not not_24 (not_24_out, S2);
  not not_25 (not_25_out, S1);
  and and_7 (and_7_out, not_25_out, not_26_out);
  not not_26 (not_26_out, S3);
  and and_8 (and_8_out, S2, not_27_out);
  not not_27 (not_27_out, S3);
  and and_9 (and_9_out, S0, S2);
  and and_10 (and_10_out, S0, S1);
  not not_28 (not_28_out, S2);
  not not_29 (not_29_out, S3);
  not not_30 (not_30_out, S0);
  and and_11 (and_11_out, not_30_out, S1);
  not not_31 (not_31_out, S2);
  not not_32 (not_32_out, S1);
  and and_12 (and_12_out, not_32_out, S2);
  and and_13 (and_13_out, S2, not_33_out);
  not not_33 (not_33_out, S3);
  not not_34 (not_34_out, S0);
  and and_14 (and_14_out, not_34_out, S1);
  not not_35 (not_35_out, S2);
  not not_36 (not_36_out, S1);
  and and_15 (and_15_out, not_1_out, not_2_out);
  and and_16 (and_16_out, not_3_out, S2);
  and and_17 (and_17_out, not_4_out, S1);
  and and_18 (and_18_out, S1, S2);
  and and_19 (and_19_out, and_1_out, not_6_out);
  not not_37 (not_37_out, S3);
  and and_20 (and_20_out, not_7_out, not_8_out);
  and and_21 (and_21_out, and_2_out, not_11_out);
  not not_38 (not_38_out, S1);
  not not_39 (not_39_out, S3);
  and and_22 (and_22_out, not_12_out, S2);
  and and_23 (and_23_out, S0, not_13_out);
  or or_1 (or_1_out, and_3_out, and_4_out);
  and and_24 (and_24_out, not_17_out, S3);
  and and_25 (and_25_out, not_18_out, S1);
  and and_26 (and_26_out, S0, not_19_out);
  and and_27 (and_27_out, and_5_out, not_22_out);
  and and_28 (and_28_out, and_6_out, S3);
  and and_29 (and_29_out, S1, not_24_out);
  and and_30 (and_30_out, S1, S2);
  not not_40 (not_40_out, S3);
  not not_41 (not_41_out, S2);
  or or_2 (or_2_out, and_7_out, and_8_out);
  or or_3 (or_3_out, and_9_out, and_10_out);
  and and_31 (and_31_out, not_28_out, not_29_out);
  and and_32 (and_32_out, and_11_out, not_31_out);
  not not_42 (not_42_out, S3);
  not not_43 (not_43_out, S1);
  or or_4 (or_4_out, and_12_out, and_13_out);
  and and_33 (and_33_out, and_14_out, not_35_out);
  and and_34 (and_34_out, S0, not_36_out);
  and and_35 (and_35_out, S0, S3);
  or or_5 (or_5_out, and_15_out, and_16_out);
  and and_36 (and_36_out, and_17_out, S3);
  or or_6 (or_6_out, and_18_out, and_19_out);
  and and_37 (and_37_out, S0, not_37_out);
  or or_7 (or_7_out, and_20_out, and_21_out);
  and and_38 (and_38_out, not_38_out, not_39_out);
  and and_39 (and_39_out, and_22_out, S3);
  and and_40 (and_40_out, and_23_out, S3);
  or or_8 (or_8_out, or_1_out, and_24_out);
  or or_9 (or_9_out, and_25_out, and_26_out);
  or or_10 (or_10_out, and_27_out, and_28_out);
  and and_41 (and_41_out, and_29_out, S3);
  and and_42 (and_42_out, and_30_out, not_40_out);
  and and_43 (and_43_out, S0, not_41_out);
  or or_11 (E, or_2_out, or_3_out);
  or or_12 (or_12_out, and_31_out, and_32_out);
  and and_44 (and_44_out, S1, not_42_out);
  and and_45 (and_45_out, S0, not_43_out);
  and and_46 (and_46_out, S0, S2);
  or or_13 (or_13_out, or_4_out, and_33_out);
  or or_14 (or_14_out, and_34_out, and_35_out);
  or or_15 (or_15_out, or_5_out, and_36_out);
  or or_16 (or_16_out, or_6_out, and_37_out);
  or or_17 (or_17_out, or_7_out, and_38_out);
  or or_18 (or_18_out, and_39_out, and_40_out);
  or or_19 (C, or_8_out, or_9_out);
  or or_20 (or_20_out, or_10_out, and_41_out);
  or or_21 (or_21_out, and_42_out, and_43_out);
  or or_22 (or_22_out, or_12_out, and_44_out);
  or or_23 (or_23_out, and_45_out, and_46_out);
  or or_24 (G, or_13_out, or_14_out);
  or or_25 (A, or_15_out, or_16_out);
  or or_26 (B, or_17_out, or_18_out);
  or or_27 (D, or_20_out, or_21_out);
  or or_28 (F, or_22_out, or_23_out);
endmodule
