// Logisim project Somador 4bits.circ as structural Verilog: 5 circuits, main circuit main
module main (
  input  X,
  input  Y,
  output Soma,
  output Vai_1
);

  xor xor_1 (Soma, X, Y);
  and and_1 (Vai_1, X, Y);
endmodule

module Somador_Completo (
  input  X,
  input  Y,
  input  Vem_1,
  output Soma,
  output Vai_1
);

  wire main_1_soma, main_1_vai_1, main_2_vai_1;

  main main_1 (.X(X), .Y(Y), .Soma(main_1_soma), .Vai_1(main_1_vai_1));
  main main_2 (.X(main_1_soma), .Y(Vem_1), .Soma(Soma), .Vai_1(main_2_vai_1));
  or or_1 (Vai_1, main_1_vai_1, main_2_vai_1);
endmodule

module Meio_Somador (
  input  X,
  input  Y,
  output Soma,
  output Vai_1
);

  xor xor_1 (Soma, X, Y);
  and and_1 (Vai_1, X, Y);
endmodule

module Somador_1bit (
  input  Vem_1,
  input  A,
  input  B,
  output Soma,
  output Vai_1
);

  wire meio_somador_1_soma, meio_somador_1_vai_1, meio_somador_2_vai_1;

  Meio_Somador meio_somador_1 (.X(A), .Y(B), .Soma(meio_somador_1_soma), .Vai_1(meio_somador_1_vai_1));
  Meio_Somador meio_somador_2 (.X(Vem_1), .Y(meio_somador_1_soma), .Soma(Soma), .Vai_1(meio_somador_2_vai_1));
  or or_1 (Vai_1, meio_somador_2_vai_1, meio_somador_1_vai_1);
endmodule

module Somador_4bits (
  input  X0,
  input  Y0,
  input  X1,
  input  Y1,
  input  X2,
  input  Y2,
  input  X3,
  input  Y3,
  output Soma_1,
  output Soma_2,
  output Soma_3,
  output Soma_4,
  output Overflow
);

  wire somador_1bit_1_vai_1, somador_1bit_2_vai_1, somador_1bit_3_vai_1, somador_1bit_4_vai_1;

  Somador_1bit somador_1bit_1 (.Vem_1(1'b0), .A(X0), .B(Y0), .Soma(Soma_1), .Vai_1(somador_1bit_1_vai_1));
  Somador_1bit somador_1bit_2 (
    .Vem_1(somador_1bit_1_vai_1), .A(X1), .B(Y1), .Soma(Soma_2), .Vai_1(somador_1bit_2_vai_1));
  Somador_1bit somador_1bit_3 (
    .Vem_1(somador_1bit_2_vai_1), .A(X2), .B(Y2), .Soma(Soma_3), .Vai_1(somador_1bit_3_vai_1));
  Somador_1bit somador_1bit_4 (
    .Vem_1(somador_1bit_3_vai_1), .A(X3), .B(Y3), .Soma(Soma_4), .Vai_1(somador_1bit_4_vai_1));
  xor xor_1 (Overflow, somador_1bit_3_vai_1, somador_1bit_4_vai_1);
endmodule
