// Logisim project ULA_LOGISIM.circ as structural Verilog: 5 circuits, main circuit main
module main (
  input  B_Inverte,
  input  A0,
  input  B0,
  input  A1,
  input  B1,
  input  A2,
  input  B2,
  input  A3,
  input  B3,
  input  Op1,
  input  Op2,
  output S0,
  output S1,
  output S2,
  output S3,
  output Carry_Out
);

  wire ula_1bit_1_carryout, ula_1bit_2_carryout, ula_1bit_3_carryout;

  ULA_1bit ula_1bit_1 (
    .A(A0), .B(B0), .B_Invert(B_Inverte), .Carry_In(B_Inverte), .CarryOut(ula_1bit_1_carryout), .Op1(Op1),
    .Op0(Op2), .\Saída (S0));
  ULA_1bit ula_1bit_2 (
    .A(A1), .B(B1), .B_Invert(B_Inverte), .Carry_In(ula_1bit_1_carryout), .CarryOut(ula_1bit_2_carryout),
    .Op1(Op1), .Op0(Op2), .\Saída (S1));
  ULA_1bit ula_1bit_3 (
    .A(A2), .B(B2), .B_Invert(B_Inverte), .Carry_In(ula_1bit_2_carryout), .CarryOut(ula_1bit_3_carryout),
    .Op1(Op1), .Op0(Op2), .\Saída (S2));
  ULA_1bit ula_1bit_4 (
    .A(A3), .B(B3), .B_Invert(B_Inverte), .Carry_In(ula_1bit_3_carryout), .CarryOut(Carry_Out), .Op1(Op1),
    .Op0(Op2), .\Saída (S3));
endmodule

module Multiplexador_2_bits (
  input  A,
  input  B,
  input  C,
  input  D,
  input  op1,
  input  op0,
  output \Saída 
);

  wire and_1_out, and_2_out, and_3_out, and_4_out, not_1_out, not_2_out, not_3_out, not_4_out;

  not not_1 (not_1_out, op1);
  not not_2 (not_2_out, op0);
  not not_3 (not_3_out, op1);
  not not_4 (not_4_out, op0);
  and and_1 (and_1_out, A, not_1_out, not_2_out);
  and and_2 (and_2_out, B, not_3_out, op0);
  and and_3 (and_3_out, C, op1, not_4_out);
  and and_4 (and_4_out, D, op1, op0);
  or or_1 (\Saída , and_1_out, and_2_out, and_3_out, and_4_out);
endmodule

module Multiplexador_1bit (
  input  A,
  input  B,
  input  Op0,
  output \Saída 
);

  wire and_1_out, and_2_out, not_1_out;

  not not_1 (not_1_out, Op0);
  and and_1 (and_1_out, A, not_1_out);
  and and_2 (and_2_out, B, Op0);
  or or_1 (\Saída , and_1_out, and_2_out);
endmodule

module Somador (
  input  Vem_1,
  input  A,
  input  B,
  output Soma,
  output Vai_1
);

  wire and_1_out, and_2_out, xor_1_out;

  xor xor_1 (xor_1_out, A, B);
  and and_1 (and_1_out, A, B);
  xor xor_2 (Soma, Vem_1, xor_1_out);
  and and_2 (and_2_out, Vem_1, xor_1_out);
  or or_1 (Vai_1, and_2_out, and_1_out);
endmodule

module ULA_1bit (
  input  B_Invert,
  input  Carry_In,
  input  A,
  input  B,
  input  Op1,
  input  Op0,
  output \Saída ,
  output CarryOut
);

  wire and_1_out, \multiplexador_1bit_1_saída , not_1_out, not_2_out, or_1_out, somador_1_soma;

  not not_1 (not_1_out, B);
  and and_1 (and_1_out, A, \multiplexador_1bit_1_saída );
  or or_1 (or_1_out, A, \multiplexador_1bit_1_saída );
  not not_2 (not_2_out, A);
  Multiplexador_1bit multiplexador_1bit_1 (
    .A(B), .B(not_1_out), .Op0(B_Invert), .\Saída (\multiplexador_1bit_1_saída ));
  Somador somador_1 (
    .A(A), .B(\multiplexador_1bit_1_saída ), .Vem_1(Carry_In), .Soma(somador_1_soma), .Vai_1(CarryOut));
  Multiplexador_2_bits multiplexador_2_bits_1 (
    .A(and_1_out), .B(or_1_out), .C(not_2_out), .D(somador_1_soma), .op1(Op1), .op0(Op0), .\Saída (\Saída ));
endmodule
